# Fritzing sketch Untitled Sketch (saved by Fritzing 0.9.5d)
breadboards: 1

parts:
  KY-1 = Keyes Relay [package=THT]
  S1 = Pushbutton [package="[SMD]"]
  S2 = Momentary Switch [package=ksa_sealed_tac_switch]
  MH-ET_LIVE_ESP32_DEVKIT1 = MH-ET LIVE ESP32 DEVKIT 38 pins
  R1 = Resistor [tolerance=±5% resistance=220 package=THT]
  LED1 = LED - 5mm [color="Red (633nm)" package="5 mm [THT]"]

nets:
  N1: KY-1.signal, LED1.cathode
  N2: KY-1.power, MH-ET_LIVE_ESP32_DEVKIT1.3V3, R1.Pin_0
  N3: KY-1.ground, MH-ET_LIVE_ESP32_DEVKIT1.GND#64
  N4: S1.Pin_1, S1.Pin_2, MH-ET_LIVE_ESP32_DEVKIT1.GND#58
  N5: S1.Pin_3, S1.Pin_4, MH-ET_LIVE_ESP32_DEVKIT1.IO13
  N6: S2.1, MH-ET_LIVE_ESP32_DEVKIT1.IO15

notes:
  GND
  3.3v
  signal

custom parts:
  Keyes Relay: The Keyes 5V relay module is suitable for SCM development, home appliance control. It uses a 5V~12V TIL control signal which can control DC / AC signal.
  MH-ET LIVE ESP32 DEVKIT 38 pins: http://mh.nodebb.com/topic/2/mh-et-live-esp32-devkit
